# Fritzing sketch button_debounce (saved by Fritzing 0.9.1b)
breadboards: 1

parts:
  Part1 = Arduino Uno (Rev3)
  S1 = Pushbutton [package="[THT]"]
  R1 = Resistor [tolerance=±5% resistance=10k package=THT]
  R2 = Resistor [tolerance=±5% resistance=220 package=THT]
  LED1 = LED - 5mm [color="Red (633nm)" package="5 mm [THT]"]

nets:
  N1: Part1.D8, R2.Pin_0
  N2: Part1.D2, S1.Pin_3, S1.Pin_4, R1.Pin_1
  N3: Part1.5V, S1.Pin_1, S1.Pin_2
  N4: Part1.GND, R1.Pin_0, LED1.cathode
  N5: R2.Pin_1, LED1.anode

// code stored in the sketch: led_blink.ino
void setup()
{

pinMode(13,OUTPUT);
}


void loop()
{
digitalWrite(13,HIGH);
delay(500);
digitalWrite(13,LOW);
delay(500);

}
